// Logisim project LC3-2200a.circ as structural Verilog
module Datapath (
  output [1:0] out_1,
  output [3:0] out_2,
  output [31:0] out_3
);

  wire checkcc_1_ccmatch, Clock, DrALU, DrPC, LdA, LdB, LdCC, LdIR, LdPC, micro_sequencer_1_drmem,
       micro_sequencer_1_droff, micro_sequencer_1_drreg, micro_sequencer_1_ldmar, not_1_out, WrMEM, WrReg;
  wire [2:0] CC_q, comparator_1_gt;
  wire [23:0] MAR_q;
  wire [31:0] A_q, alu_1_out, B_q, bit_extender_1_out, IR, LC_q, regfile_1_dout, WrMEM_out;

  Register #(.width(32)) LC (.D(out_3), .en(LdPC), .Q(LC_q), .clk(Clock));  // open: clr
  assign out_3 = DrPC ? LC_q : 32'bz;  // Controlled_Buffer controlled_buffer_1
  Register #(.width(32)) A (.D(out_3), .en(LdA), .Q(A_q), .clk(Clock));  // open: clr
  ALU alu_1 (.X(A_q), .Y(B_q), .func(out_1), .Out(alu_1_out));
  assign out_3 = DrALU ? alu_1_out : 32'bz;  // Controlled_Buffer controlled_buffer_2
  Comparator #(.width(32), .mode("unsigned")) comparator_1 (
    .a(out_3), .b({32{1'b0}}), .gt(comparator_1_gt[0]), .eq(comparator_1_gt[1]), .lt(comparator_1_gt[2]));
  Register #(.width(32)) B (.D(out_3), .en(LdB), .Q(B_q), .clk(Clock));  // open: clr
  Register #(.width(3)) CC (.D(comparator_1_gt), .en(LdCC), .Q(CC_q), .clk(Clock));  // open: clr
  Regfile regfile_1 (.Din(out_3), .WrReg(WrReg), .regno(out_2), .Clock(Clock), .Dout(regfile_1_dout));
  assign out_3 = micro_sequencer_1_drreg ? regfile_1_dout : 32'bz;  // Controlled_Buffer DrReg
  CheckCC checkcc_1 (.CC(IR[22:20]), .IR_20_22(CC_q), .CCMatch(checkcc_1_ccmatch));
  Micro_sequencer micro_sequencer_1 (
    .IR(IR), .func(out_1), .RegNo(out_2), .WrMEM(WrMEM), .CCMatch(checkcc_1_ccmatch),
    .DrReg(micro_sequencer_1_drreg), .DrMEM(micro_sequencer_1_drmem), .DrALU(DrALU), .DrPC(DrPC),
    .LdIR(LdIR), .DrOFF(micro_sequencer_1_droff), .LdPC(LdPC), .LdMAR(micro_sequencer_1_ldmar), .LdA(LdA),
    .LdB(LdB), .LdCC(LdCC), .WrREG(WrReg), .in_3(Clock));
  Register #(.width(24)) MAR (.D(out_3[23:0]), .en(micro_sequencer_1_ldmar), .Q(MAR_q), .clk(Clock));  // open: clr
  not not_1 (not_1_out, WrMEM);
  assign WrMEM_out = WrMEM ? out_3 : 32'bz;  // Controlled_Buffer WrMEM
  RAM #(.addrWidth(24), .dataWidth(32)) ram_1 (
    .addr(MAR_q), .data(WrMEM_out), .clk(Clock), .ld(not_1_out));  // open: sel, clr
  assign out_3 = micro_sequencer_1_drmem ? WrMEM_out : 32'bz;  // Controlled_Buffer DrMEM
  Register #(.width(32)) u_IR (.D(out_3), .en(LdIR), .Q(IR), .clk(Clock));  // open: clr
  assign bit_extender_1_out = {{12{IR[19]}}, IR[19:0]};  // Bit_Extender bit_extender_1
  assign out_3 = micro_sequencer_1_droff ? bit_extender_1_out : 32'bz;  // Controlled_Buffer DrOFF
  Clock clock_1 (.out(Clock));
endmodule

module ALU (
  input  [31:0] X,
  input  [31:0] Y,
  input  [1:0] func,
  output [31:0] Out
);

  wire [31:0] adder_1_out, adder_2_out, multiplexer_1_out, multiplexer_2_out, nand_1_out, shifter_1_out,
       shifter_2_out, shifter_3_out;

  Shifter #(.width(32)) shifter_1 (.in(X), .\dist (Y[4:0]), .out(shifter_1_out));
  Shifter #(.width(32), .shift("ar")) shifter_2 (.in(X), .\dist (Y[4:0]), .out(shifter_2_out));
  Multiplexer #(.width(32), .disabled(0), .enable("false")) multiplexer_1 (
    .in0(shifter_3_out), .in1(shifter_2_out), .out(multiplexer_1_out), .sel(Y[19]));
  Shifter #(.width(32), .shift("lr")) shifter_3 (.in(X), .\dist (Y[4:0]), .out(shifter_3_out));
  Adder #(.width(32)) adder_1 (.a(X), .b(Y), .out(adder_1_out), .cin(1'b0));  // open: cout
  assign nand_1_out = ~(X & Y);  // NAND_Gate nand_1, 32 bits wide
  Adder #(.width(32)) adder_2 (.a(X), .b(32'h1), .out(adder_2_out), .cin(1'b0));  // open: cout
  Multiplexer #(.width(32), .disabled(0), .enable("false")) multiplexer_2 (
    .in0(shifter_1_out), .in1(multiplexer_1_out), .out(multiplexer_2_out), .sel(Y[18]));
  Multiplexer #(.select(2), .width(32), .disabled(0), .enable("false")) multiplexer_3 (
    .in0(adder_1_out), .in1(nand_1_out), .in2(adder_2_out), .in3(multiplexer_2_out), .out(Out), .sel(func));

  // Other names for the same wires on the sheet: D = Y[18]; A = Y[19]
endmodule

module Micro_sequencer (
  input  CCMatch,
  input  [31:0] IR,
  input  in_3,
  output DrReg,
  output DrMEM,
  output DrALU,
  output DrPC,
  output LdIR,
  output DrOFF,
  output LdPC,
  output LdMAR,
  output LdA,
  output LdB,
  output LdCC,
  output WrREG,
  output WrMEM,
  output [3:0] RegNo,
  output [1:0] func
);

  wire [1:0] rom_1_data_2;
  wire [5:0] multiplexer_1_out, register_1_q, rom_2_data, rom_3_data;
  wire [24:0] rom_1_data;

  Register #(.width(6)) register_1 (.D(multiplexer_1_out), .en(1'b1), .Q(register_1_q), .clk(in_3));  // open: clr
  ROM #(.addrWidth(6), .dataWidth(25)) rom_1 (
    .addr(register_1_q),
    .data({rom_1_data[24:23], func, rom_1_data_2, WrMEM, WrREG, LdCC, LdB, LdA, LdMAR, LdIR, LdPC, DrOFF, DrPC, DrALU, DrMEM, DrReg, rom_1_data[5:0]}));  // open: sel
  Multiplexer #(.select(2), .width(6), .disabled(0), .enable("false")) multiplexer_1 (
    .in0(rom_1_data[5:0]), .in1(rom_2_data), .in2(rom_3_data), .out(multiplexer_1_out),
    .sel(rom_1_data[24:23]));  // open: in3
  ROM #(.addrWidth(4), .dataWidth(6)) rom_2 (.addr(IR[31:28]), .data(rom_2_data));  // open: sel
  Multiplexer #(.select(2), .width(4), .disabled(0), .enable("false")) multiplexer_2 (
    .in0(IR[27:24]), .in1(IR[23:20]), .in2(IR[3:0]), .out(RegNo), .sel(rom_1_data_2));  // open: in3
  ROM #(.addrWidth(2), .dataWidth(6)) rom_3 (.addr({1'b0, CCMatch}), .data(rom_3_data));  // open: sel

  // Other names for the same wires on the sheet: Clock = in_3

  // Notes on the sheet:
  //   Drives, LdPC and LdIR
  //   contents of rom_1 (hex, n*v repeats v):
  //   6201 1082 400903 800000 84045 108046 30100 84048 8409 30100 8404b 10804c 230100 1000000 420f 8410
  //   900 20212 80840 84054 8415 2116 30080 4218 8419 30100 8405b 841c 211d 40040 8405f 8420 630100 21
  //   contents of rom_2 (hex, n*v repeats v):
  //   4 7 a d 11 13 17 1a 1e 6*0 21
  //   contents of rom_3 (hex, n*v repeats v):
  //   0 e
endmodule

// Regs
module Regfile (
  input  [31:0] Din,
  input  Clock,
  input  WrReg,
  input  [3:0] regno,
  output [31:0] Dout
);

  wire a0, a1, a2, at, fp, k0, ra, s0, s1, s2, sp, t0, t1, t2, v0;
  wire [31:0] _0, _1, _2, _3, _4, _5, _6, _7, _8, _9, _10, _11, _12, _13, _14, _15;

  Demultiplexer #(.select(4), .disabled(0), .enable("false")) demultiplexer_1 (
    .out1(at), .out2(v0), .out3(a0), .out4(a1), .out5(a2), .out6(t0), .out7(t1), .out8(t2), .out9(s0),
    .out10(s1), .out11(s2), .out12(k0), .out13(sp), .out14(fp), .out15(ra), .in(WrReg), .sel(regno));  // open: out0
  Register #(.width(32)) zero (.en(1'b0), .Q(_0), .clk(Clock));  // open: D, clr
  Register #(.width(32)) u_a1 (.D(Din), .en(a1), .Q(_4), .clk(Clock));  // open: clr
  Register #(.width(32)) register_1 (.D(Din), .en(t2), .Q(_8), .clk(Clock));  // open: clr
  Register #(.width(32)) register_2 (.D(Din), .en(k0), .Q(_12), .clk(Clock));  // open: clr
  Register #(.width(32)) u_at (.D(Din), .en(at), .Q(_1), .clk(Clock));  // open: clr
  Register #(.width(32)) u_a2 (.D(Din), .en(a2), .Q(_5), .clk(Clock));  // open: clr
  Register #(.width(32)) register_3 (.D(Din), .en(s0), .Q(_9), .clk(Clock));  // open: clr
  Register #(.width(32)) register_4 (.D(Din), .en(sp), .Q(_13), .clk(Clock));  // open: clr
  Register #(.width(32)) u_v0 (.D(Din), .en(v0), .Q(_2), .clk(Clock));  // open: clr
  Register #(.width(32)) register_5 (.D(Din), .en(t0), .Q(_6), .clk(Clock));  // open: clr
  Register #(.width(32)) register_6 (.D(Din), .en(s1), .Q(_10), .clk(Clock));  // open: clr
  Register #(.width(32)) register_7 (.D(Din), .en(fp), .Q(_14), .clk(Clock));  // open: clr
  Register #(.width(32)) u_a0 (.D(Din), .en(a0), .Q(_3), .clk(Clock));  // open: clr
  Register #(.width(32)) register_8 (.D(Din), .en(t1), .Q(_7), .clk(Clock));  // open: clr
  Register #(.width(32)) register_9 (.D(Din), .en(s2), .Q(_11), .clk(Clock));  // open: clr
  Register #(.width(32)) register_10 (.D(Din), .en(ra), .Q(_15), .clk(Clock));  // open: clr
  Multiplexer #(.select(4), .width(32), .disabled(0), .enable("false")) multiplexer_1 (
    .in0(_0), .in1(_1), .in2(_2), .in3(_3), .in4(_4), .in5(_5), .in6(_6), .in7(_7), .in8(_8), .in9(_9),
    .in10(_10), .in11(_11), .in12(_12), .in13(_13), .in14(_14), .in15(_15), .out(Dout), .sel(regno));
endmodule

// ChkCC
module CheckCC (
  input  [2:0] CC,
  input  [2:0] IR_20_22,
  output CCMatch
);

  wire and_1_out, and_2_out, and_3_out;

  and and_1 (and_1_out, CC[0], IR_20_22[0]);
  and and_2 (and_2_out, CC[1], IR_20_22[1]);
  and and_3 (and_3_out, CC[2], IR_20_22[2]);
  or or_1 (CCMatch, and_1_out, and_2_out, and_3_out);
endmodule
